# Fritzing sketch B21_Schematics (saved by Fritzing 0.9.9b)
breadboards: 1

parts:
  Part1 = Arduino Uno (Rev3)
  LED1 = LEDs [package=led10mm]
  LED2 = LEDs [package=led10mm]
  R1 = Resistor [tolerance=±5% resistance=220 package="0603 [SMD]"]
  R2 = Resistor [tolerance=±5% resistance=220 package="0603 [SMD]"]
  RHT1 = Humidity and Temperature Sensor RHT03

nets:
  N1: Part1.A0, RHT1.Data-signal
  N2: Part1.D9_PWM, R2.Pin_1
  N3: Part1.D11_PWM/MOSI, R1.Pin_1
  N4: Part1.GND, LED1.C, LED2.C, RHT1.GND_2
  5V: Part1.5V, RHT1.Vcc
  N5: LED1.A, R2.Pin_0
  N6: LED2.A, R1.Pin_0
