# Fritzing sketch B23 - Schematics (saved by Fritzing 0.9.9b)
breadboards: 1

parts:
  Pololu_A1 = Pololu A4988 [package=SO16]
  M1 = Stepper Motor - Bipolar
  Part1 = Arduino Uno (Rev3) - ICSP
  BAT1 = BC9VPC [package=bc9vpc]
  U1 = POT [package=pot_mammoth]
  R1 = Resistor [tolerance=±5% resistance=220 package="0603 [SMD]"]
  S1 = Pushbutton [package="[THT]"]
  R2 = Resistor [tolerance=±5% power=0.25 resistance=10k package=THT]

nets:
  VDD: Pololu_A1.RESET, Pololu_A1.SLEEP, Pololu_A1.DIR, Pololu_A1.VDD, Part1.5V, U1.S, S1.Pin_3, S1.Pin_4
  N1: Pololu_A1.STEP, Part1.D5_PWM
  GND: Pololu_A1.GND, Part1.GND, BAT1.V-, U1.E, R2.Pin_1
  N2: Pololu_A1.1B, M1.D
  N3: Pololu_A1.1A, M1.B
  N4: Pololu_A1.2A, M1.C
  N5: Pololu_A1.2B, M1.A
  N6: Pololu_A1.VMOT, BAT1.V+
  N7: Part1.A0, R1.Pin_0
  N8: Part1.D3_PWM, S1.Pin_1, S1.Pin_2, R2.Pin_0
  N9: U1.A, R1.Pin_1
