# Fritzing sketch B24_Schematics (saved by Fritzing 0.9.9b)
breadboards: 2

parts:
  Part1 = Arduino Uno (Rev3) - ICSP
  R5 = Resistor [tolerance=±5% resistance=750 package="0603 [SMD]"]
  U4 = POT [package=pot_mammoth]
  VCC1 = Battery block 9V
  J1 = Basic Servo
  Part2 = LCD1602-I2C

nets:
  N1: Part1.A0, R5.Pin_1
  N2: Part1.D10_PWM/SS, J1.pulse
  N3: Part1.A4/SDA, Part2.SDA
  N4: Part1.A5/SCL, Part2.SCL
  5V: Part1.5V, Part2.VCC
  GND: Part1.GND, VCC1.-, J1.gnd, Part2.GND
  N5: R5.Pin_0, U4.A
  N6: VCC1.+, J1.vcc

custom parts:
  LCD1602-I2C: A standard character display, usually with 2x16 characters. Comes in many colors with LCM1602 IIC attached.
