# Fritzing sketch B26_Schematics (saved by Fritzing 0.9.9b)
breadboards: 2

parts:
  Part1 = Arduino Uno (Rev3) - ICSP
  R5 = Resistor [tolerance=±5% resistance=750 package="0603 [SMD]"]
  S1 = Pushbutton [package="[THT]"]
  Part2 = LCD1602-I2C

nets:
  N1: Part1.A4/SDA, Part2.SDA
  N2: Part1.A5/SCL, Part2.SCL
  N3: Part1.D6_PWM, R5.Pin_0, S1.Pin_1, S1.Pin_2
  5V: Part1.5V, S1.Pin_3, S1.Pin_4, Part2.VCC
  GND: Part1.GND, R5.Pin_1, Part2.GND

custom parts:
  LCD1602-I2C: A standard character display, usually with 2x16 characters. Comes in many colors with LCM1602 IIC attached.
