# Fritzing sketch B28_Schematics (saved by Fritzing 0.9.9b)
breadboards: 1

parts:
  Driver1 = 28BYJ-48 Driver Module [part_number=ULN2003 package=THT]
  SM1 = 28BYJ-48 Stepper Motor [part_number=28BYJ-48]
  Arduino = Arduino Uno (Rev3)
  U1 = POT [package=pot_mammoth]
  VCC1 = Battery block 9V
  S3 = Pushbutton [package="[THT]"]
  R3 = Resistor [tolerance=±5% power=0.25 resistance=10k package=THT]

nets:
  N1: Driver1.IN1, Arduino.D11_PWM/MOSI
  N2: Driver1.IN2, Arduino.D10_PWM/SS
  N3: Driver1.IN3, Arduino.D9_PWM
  N4: Driver1.IN4, Arduino.D8
  GND: Driver1.GND, Arduino.GND, U1.S, VCC1.-, R3.Pin_1
  N5: Driver1.Vmotor, VCC1.+
  N6: Driver1.blue-pin, SM1.blue-pin
  N7: Driver1.pink-pin, SM1.pink-pin
  N8: Driver1.yellow-pin, SM1.yellow-pin
  N9: Driver1.orange-pin, SM1.orange-pin
  N10: Driver1.red-pin, SM1.red-pin
  N11: Arduino.A0, U1.A
  N12: Arduino.D3_PWM, S3.Pin_1, S3.Pin_2, R3.Pin_0
  N13: Arduino.5V, U1.E, S3.Pin_3, S3.Pin_4

custom parts:
  28BYJ-48 Driver Module: Generic male header
  28BYJ-48 Stepper Motor: Unipolar Stepper Motor 28BYJ-48 Top coil - pink & orange Bottom coil - blue & yellow Common rail - red Connector pins: blue - pink - yellow - orange - red
